# Fritzing sketch 6809tester (saved by Fritzing 0.9.3b)
breadboards: 1

parts:
  IC1 = IC, DIP package, 40 pins [chip_label="IC                    MC6809"]
  XTAL1 = Crystal [frequency="16 Mhz" package=THT]
  C1 = Capacitor [package=cap-pth-large]
  C2 = Capacitor [package=cap-pth-large]
  Součástka1 = Breadboard Power Supply Board SMD

nets:
  GND: IC1.pin1, C1.1, C2.2, Součástka1.GND, Součástka1.VIN
  N1: IC1.pin7, IC1.pin33, IC1.pin37, IC1.pin40, Součástka1.VCC
  N2: IC1.pin38, XTAL1.pin_0, C2.1
  N3: IC1.pin39, XTAL1.pin_1, C1.2
